// Logisim project Machin2.0.circ as structural Verilog: 13 circuits, main circuit main
module main (
);

  wire button_1_out, button_2_out, button_3_out, button_4_out, button_5_out, button_6_out, button_7_out,
       button_8_out, button_9_out, button_10_out, switch_1_p2, vending_1_a, vending_1_b, vending_1_c,
       vending_1_clk, vending_1_d, vending_1_dis1, vending_1_dis2, vending_1_dis3, vending_1_e,
       vending_1_empty1, vending_1_empty2, vending_1_empty3, vending_1_f, vending_1_g, vending_1_h,
       vending_1_ttyr;
  wire [3:0] vending_1_changebcd, vending_1_changebcd_2, vending_1_changebcd_3, vending_1_dipobcd,
       vending_1_dipobcd_2, vending_1_dipobcd_3, vending_1_pro1, vending_1_pro1_2, vending_1_pro2,
       vending_1_pro2_2, vending_1_pro3, vending_1_pro3_2, vending_1_timer, vending_1_timer_2,
       vending_1_timer_3;
  wire [6:0] vending_1_ttyout;

  // Switch switch_1: pin names not known; wires that end beside it: 1'b1, switch_1_p2
  Button button_1 (.out(button_1_out));
  Button button_2 (.out(button_2_out));
  Button button_3 (.out(button_3_out));
  Button button_4 (.out(button_4_out));
  Button button_5 (.out(button_5_out));
  Button button_6 (.out(button_6_out));
  Button button_7 (.out(button_7_out));
  Button button_8 (.out(button_8_out));
  Button button_9 (.out(button_9_out));
  Button button_10 (.out(button_10_out));
  Hex_Digit_Display hex_digit_display_1 (.value(vending_1_dipobcd_3));  // open: dp
  Hex_Digit_Display hex_digit_display_2 (.value(vending_1_dipobcd_2));  // open: dp
  Hex_Digit_Display hex_digit_display_3 (.value(vending_1_dipobcd));  // open: dp
  Hex_Digit_Display hex_digit_display_4 (.value(vending_1_changebcd_3));  // open: dp
  Vending vending_1 (
    .ena(switch_1_p2), .in5(button_1_out), .in10(button_2_out), .in25(button_3_out), .Ven1(button_7_out),
    .Ven2(button_8_out), .Ven3(button_9_out), .stock1(button_4_out), .stock2(button_5_out),
    .stock3(button_6_out), .Rst(button_10_out),
    .dipoBCd({vending_1_dipobcd_3, vending_1_dipobcd_2, vending_1_dipobcd}),
    .changeBCd({vending_1_changebcd_3, vending_1_changebcd_2, vending_1_changebcd}),
    .pro1({vending_1_pro1_2, vending_1_pro1}), .pro2({vending_1_pro2_2, vending_1_pro2}),
    .pro3({vending_1_pro3_2, vending_1_pro3}), .empty1(vending_1_empty1), .empty2(vending_1_empty2),
    .empty3(vending_1_empty3), .dis1(vending_1_dis1), .dis2(vending_1_dis2), .dis3(vending_1_dis3),
    .Timer({vending_1_timer_3, vending_1_timer_2, vending_1_timer}), .A(vending_1_a), .B(vending_1_b),
    .C(vending_1_c), .D(vending_1_d), .E(vending_1_e), .F(vending_1_f), .G(vending_1_g), .H(vending_1_h),
    .ttyOut(vending_1_ttyout), .CLK(vending_1_clk), .ttyR(vending_1_ttyr));  // open: Done
  Hex_Digit_Display hex_digit_display_5 (.value(vending_1_changebcd_2));  // open: dp
  Hex_Digit_Display hex_digit_display_6 (.value(vending_1_changebcd));  // open: dp
  LED led_1 (.in(vending_1_empty1));
  LED led_2 (.in(vending_1_empty2));
  LED led_3 (.in(vending_1_empty3));
  LED led_4 (.in(vending_1_dis1));
  LED led_5 (.in(vending_1_dis2));
  LED led_6 (.in(vending_1_dis3));
  LED led_7 (.in(vending_1_a));
  LED led_8 (.in(vending_1_b));
  LED led_9 (.in(vending_1_c));
  LED led_10 (.in(vending_1_d));
  LED led_11 (.in(vending_1_e));
  LED led_12 (.in(vending_1_f));
  LED led_13 (.in(vending_1_g));
  LED led_14 (.in(vending_1_h));
  Hex_Digit_Display hex_digit_display_7 (.value(vending_1_pro1_2));  // open: dp
  Hex_Digit_Display hex_digit_display_8 (.value(vending_1_pro1));  // open: dp
  Hex_Digit_Display hex_digit_display_9 (.value(vending_1_pro2_2));  // open: dp
  Hex_Digit_Display hex_digit_display_10 (.value(vending_1_pro2));  // open: dp
  TTY #(.cols(40), .rows(15)) tty_1 (.data(vending_1_ttyout), .clk(vending_1_clk), .clr(vending_1_ttyr));  // open: we
  Hex_Digit_Display hex_digit_display_11 (.value(vending_1_pro3_2));  // open: dp
  Hex_Digit_Display hex_digit_display_12 (.value(vending_1_pro3));  // open: dp
  Hex_Digit_Display hex_digit_display_13 (.value(vending_1_timer_3));  // open: dp
  Hex_Digit_Display hex_digit_display_14 (.value(vending_1_timer_2));  // open: dp
  Hex_Digit_Display hex_digit_display_15 (.value(vending_1_timer));  // open: dp

  // Notes on the sheet:
  //   10 שקלים
  //   25 שקלים
  //   מלא מחדש
  //   5 שקלים
  //   עלות 25 שקלים
  //   עלות 50 שקלים
  //   עלות 75 שקלים
  //   מלא מחדש
  //   מלא מחדש
  //   כסף
  //   עודף
  //   מלאי 1
  //   מלאי 2
  //   מלאי 3
  //   Timer
endmodule

module Bank (
  input  In5,
  input  In10,
  input  In25,
  input  Enable,
  input  Vend1,
  input  Vend2,
  input  Vend3,
  input  Rst,
  output [7:0] OutAcc
);

  wire or_1_out, or_2_out, or_3_out;
  wire [1:0] priority_encoder_1_out;
  wire [7:0] adder_1_out, multiplexer_1_out;

  or or_1 (or_1_out, In5, In10, In25);
  or or_2 (or_2_out, Vend1, Vend2, Vend3);
  Multiplexer #(.select(2), .width(8)) multiplexer_1 (
    .in0({8{1'b0}}), .in1(8'h5), .in2(8'ha), .in3(8'h19), .out(multiplexer_1_out),
    .sel(priority_encoder_1_out));
  Priority_Encoder #(.select(2)) priority_encoder_1 (
    .in0(1'b1), .in1(In5), .in2(In10), .in3(In25), .out(priority_encoder_1_out), .en_in(Enable));  // open: gs, en_out
  Adder adder_1 (.a(OutAcc), .b(multiplexer_1_out), .out(adder_1_out));  // open: cin, cout
  or or_3 (or_3_out, or_2_out, Rst);
  Register #(.trigger("falling")) register_1 (.D(adder_1_out), .en(Enable), .clk(or_1_out), .Q(OutAcc), .clr(or_3_out));
endmodule

module Product (
  input  Restock,
  input  Vend,
  output [7:0] AvailibleBCD,
  output Empty,
  output Dispensed
);

  wire not_1_out, or_1_out;
  wire [3:0] counter_1_q;

  or or_1 (or_1_out, Restock, Vend);
  not not_1 (not_1_out, Empty);
  and and_1 (Dispensed, ~Empty, Vend);  // AND_Gate
  Counter #(.max('hf), .width(4)) counter_1 (
    .load(Restock), .up(1'b0), .count(not_1_out), .clk(or_1_out), .D(4'b1111), .carry(Empty), .Q(counter_1_q));  // open: clr
  // Binary_to_BCD_converter #(.binvalue(4)) binary_to_bcd_converter_1: pin names not known; wires that end beside it: counter_1_q, AvailibleBCD[7:4], AvailibleBCD[3:0]
endmodule

module Activator (
  input  [7:0] InCash,
  input  Vend1,
  input  Vend2,
  input  Vend3,
  input  Reset,
  input  CLK,
  output [11:0] DepositeBCD,
  output [11:0] ChangeBCD,
  output activate,
  output out_10
);

  wire and_1_out, comparator_1_eq, comparator_1_gt, comparator_1_lt, not_1_out, or_1_out;
  wire [1:0] priority_encoder_1_out;
  wire [7:0] multiplexer_1_out, multiplexer_2_out, register_1_q, register_2_q, subtractor_1_out;

  Register register_1 (.D(InCash), .clk(or_1_out), .Q(register_1_q), .clr(Reset));  // open: en
  Priority_Encoder #(.select(2)) priority_encoder_1 (
    .in0(1'b1), .in1(Vend1), .in2(Vend2), .in3(Vend3), .out(priority_encoder_1_out), .en_in(1'b1));  // open: gs, en_out
  Multiplexer #(.select(2), .width(8)) multiplexer_1 (
    .in0({8{1'b1}}), .in1(8'h19), .in2(8'h32), .in3(8'h4b), .out(multiplexer_1_out),
    .sel(priority_encoder_1_out));
  or or_1 (or_1_out, Vend1, Vend2, Vend3);
  Comparator #(.mode("unsigned")) comparator_1 (
    .a(register_1_q), .b(multiplexer_1_out), .gt(comparator_1_gt), .eq(comparator_1_eq), .lt(comparator_1_lt));
  // Binary_to_BCD_converter #(.binvalue(8)) binary_to_bcd_converter_1: pin names not known; wires that end beside it: InCash, DepositeBCD[11:8], DepositeBCD[7:4], DepositeBCD[3:0]
  Multiplexer #(.width(8)) multiplexer_2 (
    .in0(multiplexer_1_out), .in1(register_1_q), .out(multiplexer_2_out), .sel(comparator_1_gt));
  Subtractor subtractor_1 (.a(multiplexer_2_out), .b(multiplexer_1_out), .out(subtractor_1_out));  // open: bin, bout
  or or_2 (activate, comparator_1_gt, comparator_1_eq);
  Register register_2 (.D(subtractor_1_out), .clk(not_1_out), .Q(register_2_q), .clr(Reset));  // open: en
  not not_1 (not_1_out, or_1_out);
  and and_1 (and_1_out, comparator_1_lt, or_1_out);
  // Binary_to_BCD_converter #(.binvalue(8)) binary_to_bcd_converter_2: pin names not known; wires that end beside it: register_2_q, ChangeBCD[11:8], ChangeBCD[7:4], ChangeBCD[3:0]
  EdgeTrigger edgetrigger_1 (.D(and_1_out), .Clk(CLK), .Reset(Reset), .Q(out_10));

  // Other names for the same wires on the sheet: R = Reset
endmodule

module Dispenser (
  input  Activate,
  input  Vend01,
  input  Vend02,
  input  Vend03,
  input  Restock01,
  input  Restock02,
  input  Restock03,
  output [7:0] Availible1,
  output [7:0] Availible2,
  output [7:0] Availible3,
  output Empty1,
  output Empty2,
  output Empty3,
  output Dispenes1,
  output Dispenes2,
  output Dispenes3
);

  wire demultiplexer_1_out1, demultiplexer_1_out2, demultiplexer_1_out3;
  wire [1:0] priority_encoder_1_out;

  Demultiplexer #(.select(2)) demultiplexer_1 (
    .out1(demultiplexer_1_out1), .out2(demultiplexer_1_out2), .out3(demultiplexer_1_out3), .in(Activate),
    .sel(priority_encoder_1_out));  // open: out0
  Priority_Encoder #(.select(2)) priority_encoder_1 (
    .in0(1'b1), .in1(Vend01), .in2(Vend02), .in3(Vend03), .out(priority_encoder_1_out), .en_in(1'b1));  // open: gs, en_out
  Product product_1 (
    .Restock(Restock01), .Vend(demultiplexer_1_out1), .AvailibleBCD(Availible1), .Empty(Empty1),
    .Dispensed(Dispenes1));
  Product product_2 (
    .Restock(Restock02), .Vend(demultiplexer_1_out2), .AvailibleBCD(Availible2), .Empty(Empty2),
    .Dispensed(Dispenes2));
  Product product_3 (
    .Restock(Restock03), .Vend(demultiplexer_1_out3), .AvailibleBCD(Availible3), .Empty(Empty3),
    .Dispensed(Dispenes3));
endmodule

module NotEmpty (
  input  [7:0] in_1,
  input  Vend,
  output Buy,
  output Empty
);

  wire comparator_1_gt;

  Comparator #(.mode("unsigned")) comparator_1 (.a(in_1), .b({8{1'b0}}), .gt(comparator_1_gt), .eq(Empty));  // open: lt
  and and_1 (Buy, comparator_1_gt, Vend);
endmodule

module timer (
  input  Rst,
  input  Up,
  input  [7:0] Min,
  input  [7:0] Max,
  input  CLK,
  input  stop,
  output [7:0] OutBin,
  output [11:0] OutBCD,
  output Done,
  output Active
);

  wire and_1_out, and_2_out, and_3_out, comparator_1_eq, comparator_2_eq, comparator_2_gt, comparator_3_eq,
       comparator_3_lt, or_1_out, or_2_out;
  wire [7:0] multiplexer_1_out, multiplexer_2_out;

  and and_1 (and_1_out, CLK, ~stop);  // AND_Gate
  Multiplexer #(.width(8)) multiplexer_1 (.in0(Max), .in1(Min), .out(multiplexer_1_out), .sel(Up));
  Multiplexer #(.width(8)) multiplexer_2 (.in0(Min), .in1(Max), .out(multiplexer_2_out), .sel(Up));
  Comparator comparator_1 (.a(multiplexer_2_out), .b(OutBin), .eq(comparator_1_eq));  // open: gt, lt
  or or_1 (or_1_out, Rst, comparator_1_eq);
  or or_2 (or_2_out, Rst, and_1_out);
  Counter counter_1 (
    .load(or_1_out), .up(Up), .clk(or_2_out), .D(multiplexer_1_out), .Q(OutBin));  // open: clr, count, carry
  Comparator comparator_2 (.a(OutBin), .b(Min), .gt(comparator_2_gt), .eq(comparator_2_eq));  // open: lt
  Comparator comparator_3 (.a(OutBin), .b(Max), .eq(comparator_3_eq), .lt(comparator_3_lt));  // open: gt
  // Binary_to_BCD_converter #(.binvalue(8)) binary_to_bcd_converter_1: pin names not known; wires that end beside it: OutBin, OutBCD[11:8], OutBCD[7:4], OutBCD[3:0]
  and and_2 (and_2_out, comparator_2_eq, ~Up);  // AND_Gate
  and and_3 (and_3_out, comparator_3_eq, Up);
  or or_3 (Done, and_2_out, and_3_out);
  and and_4 (Active, comparator_2_gt, comparator_3_lt);
endmodule

module SUM (
  input  [7:0] In1,
  input  [7:0] In2,
  input  [7:0] In3,
  input  [7:0] In4,
  input  [7:0] In5,
  input  [7:0] In6,
  input  [7:0] In7,
  input  [7:0] In8,
  output [7:0] out_9
);

  wire [7:0] adder_1_out, adder_2_out, adder_3_out, adder_4_out, adder_5_out, adder_6_out;

  Adder adder_1 (.a(In1), .b(In2), .out(adder_1_out));  // open: cin, cout
  Adder adder_2 (.a(adder_1_out), .b(In3), .out(adder_2_out));  // open: cin, cout
  Adder adder_3 (.a(adder_2_out), .b(In4), .out(adder_3_out));  // open: cin, cout
  Adder adder_4 (.a(adder_3_out), .b(In5), .out(adder_4_out));  // open: cin, cout
  Adder adder_5 (.a(adder_4_out), .b(In6), .out(adder_5_out));  // open: cin, cout
  Adder adder_6 (.a(adder_5_out), .b(In7), .out(adder_6_out));  // open: cin, cout
  Adder adder_7 (.a(adder_6_out), .b(In8), .out(out_9));  // open: cin, cout
endmodule

module pogram (
  input  Reset,
  input  P1,
  input  P2,
  input  P3,
  input  CLK,
  output [11:0] TotalTimeBCD,
  output M1,
  output M2,
  output M3,
  output M4,
  output M5,
  output M6,
  output M7,
  output M8,
  output Done
);

  wire A_done, d_ff_1_q, d_ff_2_q, d_ff_3_q, edgetrigger_1_q, edgetrigger_2_q, edgetrigger_3_q, not_1_out,
       or_1_out, or_4_out, R, R2, timer_1_done, timer_2_done, timer_3_done, timer_4_done, timer_5_done,
       timer_6_done, timer_7_done, xnor_1_out, xnor_2_out, xnor_3_out, xnor_4_out, xnor_5_out, xnor_6_out,
       xnor_7_out;
  wire [2:0] priority_encoder_1_out;
  wire [7:0] multiplexer_1_out, register_1_q, sum_1_out_9, timer_7_outbin, timer_8_outbin;
  wire [11:0] A_outbcd, timer_1_outbcd, timer_2_outbcd, timer_3_outbcd, timer_4_outbcd, timer_5_outbcd,
       timer_6_outbcd, timer_7_outbcd;
  wire [63:0] rom_1_data;

  or or_1 (or_1_out, P1, P2, P3);
  D_Flip_Flop d_ff_1 (.D(P1), .clk(P1), .Q(d_ff_1_q), .reset(R));  // open: Qn, preset
  D_Flip_Flop d_ff_2 (.D(P2), .clk(P2), .Q(d_ff_2_q), .reset(R));  // open: Qn, preset
  D_Flip_Flop d_ff_3 (.D(P3), .clk(P3), .Q(d_ff_3_q), .reset(R));  // open: Qn, preset
  or or_2 (R, Reset, edgetrigger_1_q);
  EdgeTrigger edgetrigger_1 (.D(Done), .Clk(CLK), .Reset(Reset), .Q(edgetrigger_1_q));
  Priority_Encoder priority_encoder_1 (
    .in0(1'b1), .in1(d_ff_1_q), .in2(d_ff_2_q), .in3(d_ff_3_q), .out(priority_encoder_1_out), .en_in(1'b1));  // open: in4, in5, in6, in7, gs, en_out
  EdgeTrigger edgetrigger_2 (.D(or_1_out), .Clk(CLK), .Reset(R), .Q(edgetrigger_2_q));
  Multiplexer #(.select(3), .width(8)) multiplexer_1 (
    .in0({8{1'b0}}), .in1(8'h4), .in2(8'h8), .in3(8'hc), .out(multiplexer_1_out), .sel(priority_encoder_1_out));  // open: in4, in5, in6, in7
  or or_3 (R2, edgetrigger_2_q, R);
  ROM #(.dataWidth(64)) rom_1 (.addr(multiplexer_1_out), .data(rom_1_data));
  // Probe on rom_1_data[63:56]
  // Probe on rom_1_data[55:48]
  // Probe on rom_1_data[47:40]
  // Probe on rom_1_data[39:32]
  // Probe on rom_1_data[31:24]
  // Probe on rom_1_data[23:16]
  // Probe on rom_1_data[15:8]
  // Probe on rom_1_data[7:0]
  timer A (
    .Rst(R2), .Up(1'b1), .Min({8{1'b0}}), .Max(rom_1_data[7:0]), .CLK(CLK), .stop(A_done), .OutBCD(A_outbcd),
    .Done(A_done), .Active(M1));  // open: OutBin
  // Probe on A_outbcd
  timer timer_1 (
    .Rst(R2), .Up(1'b1), .Min({8{1'b0}}), .Max(rom_1_data[15:8]), .CLK(CLK), .stop(xnor_4_out),
    .OutBCD(timer_1_outbcd), .Done(timer_1_done), .Active(M2));  // open: OutBin
  // Probe on timer_1_outbcd
  timer timer_2 (
    .Rst(R2), .Up(1'b1), .Min({8{1'b0}}), .Max(rom_1_data[23:16]), .CLK(CLK), .stop(xnor_5_out),
    .OutBCD(timer_2_outbcd), .Done(timer_2_done), .Active(M3));  // open: OutBin
  // Probe on timer_2_outbcd
  timer timer_3 (
    .Rst(R2), .Up(1'b1), .Min({8{1'b0}}), .Max(rom_1_data[31:24]), .CLK(CLK), .stop(xnor_1_out),
    .OutBCD(timer_3_outbcd), .Done(timer_3_done), .Active(M4));  // open: OutBin
  // Probe on timer_3_outbcd
  xnor xnor_1 (xnor_1_out, timer_3_done, timer_2_done);
  timer timer_4 (
    .Rst(R2), .Up(1'b1), .Min({8{1'b0}}), .Max(rom_1_data[39:32]), .CLK(CLK), .stop(xnor_6_out),
    .OutBCD(timer_4_outbcd), .Done(timer_4_done), .Active(M5));  // open: OutBin
  // Probe on timer_4_outbcd
  timer timer_5 (
    .Rst(R2), .Up(1'b1), .Min({8{1'b0}}), .Max(rom_1_data[47:40]), .CLK(CLK), .stop(xnor_2_out),
    .OutBCD(timer_5_outbcd), .Done(timer_5_done), .Active(M6));  // open: OutBin
  // Probe on timer_5_outbcd
  xnor xnor_2 (xnor_2_out, timer_5_done, timer_4_done);
  timer timer_6 (
    .Rst(R2), .Up(1'b1), .Min({8{1'b0}}), .Max(rom_1_data[55:48]), .CLK(CLK), .stop(xnor_7_out),
    .OutBCD(timer_6_outbcd), .Done(timer_6_done), .Active(M7));  // open: OutBin
  // Probe on timer_6_outbcd
  timer timer_7 (
    .Rst(R2), .Up(1'b1), .Min({8{1'b0}}), .Max(rom_1_data[63:56]), .CLK(CLK), .stop(xnor_3_out),
    .OutBin(timer_7_outbin), .OutBCD(timer_7_outbcd), .Done(timer_7_done), .Active(M8));
  // Probe on timer_7_outbcd
  xnor xnor_3 (xnor_3_out, timer_7_done, timer_6_done);
  xnor xnor_4 (xnor_4_out, timer_1_done, A_done);
  xnor xnor_5 (xnor_5_out, timer_2_done, timer_1_done);
  xnor xnor_6 (xnor_6_out, timer_4_done, timer_3_done);
  xnor xnor_7 (xnor_7_out, timer_6_done, timer_5_done);
  LED led_1 (.in(M8));
  LED led_2 (.in(M1));
  LED led_3 (.in(M2));
  LED led_4 (.in(M3));
  LED led_5 (.in(M4));
  LED led_6 (.in(M5));
  LED led_7 (.in(M6));
  LED led_8 (.in(M7));
  not not_1 (not_1_out, CLK);
  SUM sum_1 (
    .In1(rom_1_data[63:56]), .In2(rom_1_data[55:48]), .In3(rom_1_data[47:40]), .In4(rom_1_data[39:32]),
    .In5(rom_1_data[31:24]), .In6(rom_1_data[23:16]), .In7(rom_1_data[15:8]), .In8(rom_1_data[7:0]),
    .out_9(sum_1_out_9));
  Register register_1 (.D(sum_1_out_9), .clk(CLK), .Q(register_1_q), .clr(edgetrigger_3_q));  // open: en
  EdgeTrigger edgetrigger_3 (.D(Done), .Clk(not_1_out), .Reset(R), .Q(edgetrigger_3_q));
  or or_4 (or_4_out, R, R2);
  timer timer_8 (
    .Rst(or_4_out), .Up(1'b0), .Min({8{1'b0}}), .Max(register_1_q), .CLK(CLK), .stop(Done),
    .OutBin(timer_8_outbin), .OutBCD(TotalTimeBCD), .Done(Done));  // open: Active
  // Probe on timer_8_outbin
  Hex_Digit_Display hex_digit_display_1 (.value(TotalTimeBCD[11:8]));  // open: dp
  Hex_Digit_Display hex_digit_display_2 (.value(TotalTimeBCD[7:4]));  // open: dp
  Hex_Digit_Display hex_digit_display_3 (.value(TotalTimeBCD[3:0]));  // open: dp

  // Other names for the same wires on the sheet: A = M1; B = M2; C = M3; D = M4; E = M5; F = M6; G = M7; H = M8

  // Notes on the sheet:
  //   contents of rom_1 (hex, n*v repeats v):
  //   4*0 6401320101011901 0 0 0 6401191901013201 0 0 0 807060504030201 75efe363 2b45309a 5ee78b5c
  //   6ba2eb71 11b77fbb ffffffffc80678f4 4ea8c88e 28642179 2dbbf1d1 ffffffffb594b7c9 464ed148
  //   ffffffffd58e0516 61f8558f ffffffffd521802c ffffffffd269b26f ffffffff9c92c3e7 5f457e72
  //   ffffffffcb7a78e4 ffffffffc6d295b8 ffffffff9e81a67b 3479d60b 9cc9eec 675b0831 ffffffffecabfad7
  //   ffffffffab368a82 519d57f1 33ae90b9 680ccef5 ffffffffe6bc0d0e ffffffff96e354d7 ffffffff8c609683
  //   6efd7b3f ffffffffa05fe07e ffffffffd6694435 6c609797 ffffffffe800fd18 767db7b3 51e454d4
  //   ffffffffdf4eaf51 ffffffff87b02153 ffffffffc3fde423 ffffffffa6688833 ffffffffb26a6ce0 27107eba
  //   5fcb1458 5d24d506 1b15f9c8 ffffffff9ee04088 74d1626f ffffffffe99119b3 ffffffffb3279061
  //   ffffffffe3a0c0ef 5c60b29a ffffffff8377ded4 38834255 d69f394 60c619e ffffffffee85e9b7
  //   fffffffff2b70f26 ffffffff8dd0a00e 1624356 c499ee1 7e934aa6 15696c6a ffffffffaf12f12e 8cc3487 4f9537c
  //   ffffffff91b2b7aa 786568a8 d2eb513 ffffffff8f5a99a6 3b6f4441 2d0ff9db ffffffffa6f4d1a5 41a1f4f2
  //   ffffffffe4bbb298 ffffffffd0d085ef 7de7848f ffffffffbe814b83 ffffffff9568cb8d 335e0da2
  //   ffffffff85b983d8 ffffffffe05d8852 b649aef ffffffffa68d8fc6 ffffffff93d783ba 3e52e1ab
  //   ffffffffe43c5a03 7c437c0 250e4925 ffffffffaa0b6fac c012a02 1b10dc0b 29f08c3a fffffffff06212c9
  //   ffffffff8d199e98 ffffffffe786ccb3 ffffffffe426aad0 ffffffffac0baa4b 3ca1867 5db3f1db 3a122af2
  //   ffffffffe6c09acc ffffffffc77def82 124c3a37 696f0d5e ffffffff9aa0a4bc 531b6df2 40645992
  //   ffffffffacdcf008 ffffffffe2cb0adf ffffffff94ec9a35 ffffffff97d5d74a 3b7a0095 ffffffffcf6508cd
  //   ffffffff95e6d1ba ffffffff95a66ccf 4f9bee1 5e889971 575b3366 458cb428 ffffffffafe18f79 10d58d8b
  //   ffffffffdd59da12 54ec266d ffffffffaad51e21 ffffffffed9ef22e 1b51e70a 50e26a4e ffffffff951c9050
  //   ffffffff8feec742 ffffffffdfb85c8f ffffffffc23ff28a ffffffffddce87af 2da0603 ffffffffeabfc856
  //   ffffffff9b85ec79 3c47f49e ffffffffc8def780 136abe08 16437e83 ffffffff8fdbb8af 6747db1d
  //   ffffffffbd8321c0 ffffffffae6c56a7 ffffffffc7e41929 33cbdd11 ffffffffea404290 638288f5
  //   ffffffffb0a00186 ffffffffefe85ce9 ffffffffdca5c4fc ffffffffc8adbe14 ffffffffe48615f5
  //   fffffffff2ac8403 ffffffffa1e55d7d ffffffffb619b1bd ffffffffacf795d9 3ef12c14 ffffffffcd4d5aff
  //   ffffffff9f36013d 507d0e48 ffffffffe93715a3 5e8e0163 ffffffffaab149f7 27f6dc8c ffffffff9da56e8b
  //   185fb3fe ffffffffaa4997e0 ffffffffd76b80a6 ffffffffebe2a87d ffffffff84d3f018 fffffffff9cc2402
  //   325dbfc6 3bc19f7c ffffffff83db176e 1dde62f9 ffffffffa6d496d4 fffffffff2fd105f ffffffff87c90ab1
  //   ffffffffb46a6379 ffffffff857efceb 617b5f52 ffffffff92e29405 ffffffffe9c87cc6 209d75d8 7ed4ae55
  //   ffffffffa03da183 2f004d3a ffffffff869b749f 611543bb 617e4fb7 5ebb08c2 ffffffff90828df6
  //   ffffffff99f640ad 223ac422 ffffffffd7c11761 17b17ac9 5506a7a5 310fd7b9 551d03ac 6980eab4 267eb2f3
  //   65b09164 753db94d 7ac0268c fffffffff7b77b3b 3a7a7080 fffffffff2b21381 fffffffff03382d6 6380edf5
  //   7758875e ffffffff8a57bb9a ffffffffcc7ea24e 21d013ec ffffffff9aff65c1 6c17577d 77248862
  //   ffffffffd77fa7c0 6cbd364 ffffffffdc880824 ffffffffdb877bb5 ffffffffbc1cfc64 70ce5a72 5f14381d
  //   ffffffff9212b89c cfb33a0 46cda20c 5979ba09 60f7f3a4 3206c490 7c4998c7 ffffffffa2bf371e
  //   ffffffffe52aac0a ffffffffce135223 ffffffffb4c96f2b ffffffffd8f8eda6 ffffffffdf834e41
  //   ffffffffb19dd19d ffffffffdafe6235 ffffffffaa76bf7e 75342670 ffffffffcc3d0115
endmodule

module EdgeTrigger (
  input  D,
  input  Clk,
  input  Reset,
  output Q
);

  wire and_1_out, d_ff_1_q, d_ff_2_q, d_ff_3_q, not_1_out, not_2_out;

  D_Flip_Flop d_ff_1 (.D(D), .clk(D), .Q(d_ff_1_q), .reset(Q));  // open: Qn, preset
  and and_1 (and_1_out, d_ff_1_q, not_2_out);
  D_Flip_Flop d_ff_2 (.D(and_1_out), .clk(Clk), .Q(d_ff_2_q));  // open: Qn, preset, reset
  not not_1 (not_1_out, Clk);
  not not_2 (not_2_out, d_ff_3_q);
  D_Flip_Flop d_ff_3 (.D(d_ff_2_q), .clk(not_1_out), .Q(d_ff_3_q), .reset(Reset));  // open: Qn, preset
  and and_2 (Q, d_ff_2_q, d_ff_3_q);
  // Digital_Oscilloscope digital_oscilloscope_1: pin names not known; wires that end beside it: Clk, Q

  // Other names for the same wires on the sheet: R = Reset
endmodule

module message (
  input  Rst,
  input  in1,
  input  in2,
  input  in3,
  input  in4,
  input  in5,
  input  in6,
  input  in7,
  input  Clk,
  output [6:0] ttyOut
);

  wire ena, load, or_1_out;
  wire [2:0] priority_encoder_1_out;
  wire [7:7] rom_1_data;
  wire [23:0] adder_1_out, counter_1_q, multiplexer_1_out;

  and and_1 (load, Rst, ~ena);  // AND_Gate
  or or_1 (or_1_out, Clk, load);
  Counter #(.max('hffffff), .width(24)) counter_1 (
    .clr(Rst), .load(load), .count(ena), .clk(or_1_out), .D({24{1'b0}}), .Q(counter_1_q));  // open: up, carry
  Priority_Encoder priority_encoder_1 (
    .in0(1'b1), .in1(in1), .in2(in2), .in3(in3), .in4(in4), .in5(in5), .in6(in6), .in7(in7),
    .out(priority_encoder_1_out), .en_in(1'b1));  // open: gs, en_out
  Multiplexer #(.select(3), .width(24)) multiplexer_1 (
    .in0({24{1'b0}}), .in1(24'h10), .in2(24'hb0), .in3(24'h150), .in4(24'h1e0), .in5(24'h250), .in6(24'h2b0),
    .in7(24'h320), .out(multiplexer_1_out), .sel(priority_encoder_1_out));
  Adder #(.width(24)) adder_1 (.a(counter_1_q), .b(multiplexer_1_out), .out(adder_1_out));  // open: cin, cout
  ROM #(.addrWidth(24)) rom_1 (.addr(adder_1_out), .data({rom_1_data[7], ttyOut}));
  BitFinder bitfinder_1 (.in({rom_1_data[7], ttyOut}), .found(ena));  // open: index
  TTY tty_1 (.data(ttyOut), .clk(Clk), .clr(Rst));  // open: we

  // Other names for the same wires on the sheet: CtrClk = Clk

  // Notes on the sheet:
  //   contents of rom_1 (hex, n*v repeats v):
  //   16*0 68 65 6c 6c 6f a 79 6f 75 20 68 61 76 65 20 63 68 6f 73 65 6e 20 70 72 6f 67 72 61 6d 20 6e 75
  //   6d 62 65 72 20 31 a 74 68 65 20 63 6f 73 74 20 69 73 20 32 35 20 49 4c 53 20 a 66 6f 72 20 74 68 65
  //   20 64 75 72 61 74 69 6f 6e 20 69 73 20 31 38 30 20 6d 69 6e 75 74 65 73 a 54 68 61 6e 6b 20 79 6f 75
  //   20 66 6f 72 20 62 75 79 69 6e 67 20 a 68 61 76 65 20 61 20 67 6f 6f 64 20 64 61 79 20 31*0 68 65 6c
  //   6c 6f a 79 6f 75 20 68 61 76 65 20 63 68 6f 73 65 6e 20 70 72 6f 67 72 61 6d 20 6e 75 6d 62 65 72 20
  //   32 a 74 68 65 20 63 6f 73 74 20 69 73 20 35 30 20 49 4c 53 20 a 66 6f 72 20 74 68 65 20 64 75 72 61
  //   74 69 6f 6e 20 69 73 20 32 30 34 20 6d 69 6e 75 74 65 73 a 54 68 61 6e 6b 20 79 6f 75 20 66 6f 72 20
  //   62 75 79 69 6e 67 20 a 68 61 76 65 20 61 20 67 6f 6f 64 20 64 61 79 20 31*0 68 65 6c 6c 6f a 79 6f
  //   75 20 68 61 76 65 20 63 68 6f 73 65 6e 20 70 72 6f 67 72 61 6d 20 6e 75 6d 62 65 72 20 33 a 74 68 65
  //   20 63 6f 73 74 20 69 73 20 37 35 20 49 4c 53 20 a 66 6f 72 20 74 68 65 20 64 75 72 61 74 69 6f 6e 20
  //   69 73 20 33 36 20 6d 69 6e 75 74 65 73 a 54 68 61 6e 6b 20 79 6f 75 20 66 6f 72 20 62 75 79 69 6e 67
  //   20 a 68 61 76 65 20 61 20 67 6f 6f 64 20 64 61 79 20 16*0 54 68 65 72 65 20 64 6f 65 73 20 6e 6f 74
  //   20 73 65 65 6d 20 74 6f 20 62 65 20 65 6e 6f 75 67 68 20 6d 6f 6e 65 79 20 66 6f 72 20 74 68 69 73
  //   20 70 72 6f 67 72 61 6d a 50 6c 65 61 73 65 20 74 72 79 20 61 67 61 69 6e a 67 6f 6f 64 20 64 61 79
  //   31*0 49 6e 76 65 6e 74 6f 72 79 20 66 6f 72 20 74 68 69 73 20 70 72 6f 67 72 61 6d 20 73 65 65 6d 73
  //   20 74 6f 20 68 61 76 65 20 72 75 6e 20 6f 75 74 a 50 6c 65 61 73 65 20 74 72 79 20 61 67 61 69 6e a
  //   67 6f 6f 64 20 64 61 79 22*0 49 6e 76 65 6e 74 6f 72 79 20 66 6f 72 20 74 68 69 73 20 70 72 6f 67 72
  //   61 6d 20 73 65 65 6d 73 20 74 6f 20 68 61 76 65 20 72 75 6e 20 6f 75 74 a 50 6c 65 61 73 65 20 74 72
  //   79 20 61 67 61 69 6e a 67 6f 6f 64 20 64 61 79 38*0 49 6e 76 65 6e 74 6f 72 79 20 66 6f 72 20 74 68
  //   69 73 20 70 72 6f 67 72 61 6d 20 73 65 65 6d 73 20 74 6f 20 68 61 76 65 20 72 75 6e 20 6f 75 74 a 50
  //   6c 65 61 73 65 20 74 72 79 20 61 67 61 69 6e a 67 6f 6f 64 20 64 61 79 3 c6 b2 35 2e 66 9f bd 79 20
  //   e8 b0 4 aa 26 aa 56 26 1c 8c 21 12 2b 56 cf 3c c4 cb 67 18 8b 5b 8c 3 79 ed 35 b3 ea e5 99 34 2b 52
  //   24 d d0 5c 35 f1 56 dc f8 84 e9 8d 33 a0 9e df db 45 2b 87 c5 cb 6a 94 61 91 a 7f d5 4 d3 13 8 b2 4
  //   fb 66 27 46 6c aa 30 f1 b8 a5 99 4a 87 71 85 9 2a dc 53 85 50 a8 8 55 eb b6 9a d0 32 11 31 5f 19 c1
  //   37 50 e4 26 b3 2a 81 7c 13 c9 81 b a 5f 63 d8 9a 39 26 e2 61 24 cb 6a 5b 6d 88 73 93 a5 b6 41 a4 bd
  //   a3 30 20 83 ca c6 9d 69 10 8 b0 54 d5 b8 a4 e8 99 5e 91 32 43 f1 2a 84 6c 30 32 e5 6e 45 65 f4 8d 5f
  //   41 92 f0 9d 7a 37 51 b5 85 e0 32 f0 a5 e8 3f 5f e9 97 f6 c2 8 5d 20 2e 78 46 a 68 74 6f fc 3a 4a 1
  //   1a 3b 7b 62 61 11 5a a4 67 b8 8f 90 b8 3 6f d1 37 69 c2 a7 50 c6 ef 4 e7 6b fc f1 69 9 80 55 fc 42
  //   1a f0 cf 55 f0 35 e9 be 81 bf 9b 16 77 5b 0 9e 1e 17 15 67 22 28 be c5 ae 83 33 c9 5c 77 9a c0 5d 5f
  //   dd cc 32 56 95 a6 a0 63 ca 4b e7 59 23 52 11 21 e bb da 68 4a 3f b6 a9 26 c8 98 a2 85 69 f9 a2 6 6c
  //   f a1 b7 eb d1 84 b6 5d b4 d0 39 3a 73 5b 2 d9 2b b8 44 33 e1 61 1b 6f b8 c 1c 92 43 ff 5d b8 60 25
  //   a8 99 dc 51 11 9b 1a fa c8 4f c4 fb 91 fe d9 12 48 de 59 5b 57 ae 8b f1 41 57 5c 51 34 77 66 72 8a
  //   58 6e aa 67 5c fc 1a 32 cc 6b f6 6c 51 8e eb c 4d 90 f8 9 9b 19 68 11 88 26 26 87 a1 5f 98 a3 59 88
  //   ad 2c e0 5 71 d3 1c fc 43 a6 2f 6a d7 79 62 ce 87 7e ac 89 8a 18 ca 83 43 c5 29 ac 96 d1 96 cc c8 b4
  //   11 f9 ba ea 4d a bc 81 7d 64 e4 20 76 e2 44 7e 2b 83 65 83 68 50 9 57 fd e b7 a2 f1 31 c3 92 b8 b9
  //   bb b1 72 f6 24 5a 89 4 20 8d e 7a 97 54 42 78 4e c9 71 ad 32 7f e2 7c 6a 82 a5 a2 55 f1 8f 81 67 3e
  //   7f 44 c9 15 ef ec d6 f4 2b a0 15 d 3d 6f f2 57 77 3 7f f9 85 3 fb 88 94 f4 af 4b cb d6 11 97 28 fd
  //   4b 9c 8 bd f1 bf b9 d7 c3 53 6f bc c5 bc 9d 55 b6 f5 69 4a ce 62 ee d2 97 19 7d af 2c 8e 2b 8a ff e9
  //   65 cb 23 7a 8c 68 16 88 3e 32 40 c7 4f 53 8f d4 b 1d 80 dd b1 1 71 e8 6f 49 24 d0 9c 9d 7d 1f d1 2b
  //   27 91 7f 47 38 7f e0 46 67 2a 38 b1 f7 37 e0 96 7a 88 81 90 de 61 d9 3d bf b4 a9 9a c2 2c 57 9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
endmodule

module Vending (
  input  ena,
  input  in5,
  input  in10,
  input  in25,
  input  Ven1,
  input  Ven2,
  input  Ven3,
  input  stock1,
  input  stock2,
  input  stock3,
  input  Rst,
  output [11:0] dipoBCd,
  output [11:0] changeBCd,
  output [7:0] pro1,
  output [7:0] pro2,
  output [7:0] pro3,
  output empty1,
  output empty2,
  output empty3,
  output dis1,
  output dis2,
  output dis3,
  output [11:0] Timer,
  output A,
  output B,
  output C,
  output D,
  output E,
  output F,
  output G,
  output H,
  output Done,
  output [6:0] ttyOut,
  output CLK,
  output ttyR
);

  wire and_1_out, Clk8_out, d_ff_1_q, d_ff_2_q, d_ff_3_q, d_ff_5_q, d_ff_6_q, d_ff_7_q, d_ff_8_q, E1, E2, E3,
       edgetrigger_1_q, ENA_t, N, or_1_out, V1, V2, V3;
  wire [7:0] bank_1_outacc;

  Clock clock_1 (.out(CLK));
  NotEmpty notempty_1 (.in_1(pro1), .Vend(Ven1), .Buy(V1), .Empty(E1));
  NotEmpty notempty_2 (.in_1(pro2), .Vend(Ven2), .Buy(V2), .Empty(E2));
  NotEmpty notempty_3 (.in_1(pro3), .Vend(Ven3), .Buy(V3), .Empty(E3));
  Clock #(.highDuration(8), .lowDuration(8)) Clk8 (.out(Clk8_out));
  Bank bank_1 (
    .In5(in5), .In10(in10), .In25(in25), .Enable(ena), .Vend1(V1), .Vend2(V2), .Vend3(V3), .Rst(Rst),
    .OutAcc(bank_1_outacc));
  EdgeTrigger edgetrigger_1 (.D(ENA_t), .Clk(Clk8_out), .Reset(Rst), .Q(edgetrigger_1_q));
  D_Flip_Flop d_ff_1 (.D(V1), .clk(V1), .Q(d_ff_1_q), .reset(Rst));  // open: Qn, preset
  D_Flip_Flop d_ff_2 (.D(V2), .clk(V2), .Q(d_ff_2_q), .reset(Rst));  // open: Qn, preset
  D_Flip_Flop d_ff_3 (.D(V3), .clk(V3), .Q(d_ff_3_q), .reset(Rst));  // open: Qn, preset
  D_Flip_Flop d_ff_4 (.D(N), .clk(N), .reset(Rst));  // open: Q, Qn, preset
  D_Flip_Flop d_ff_5 (.D(E1), .clk(E1), .Q(d_ff_5_q), .reset(Rst));  // open: Qn, preset
  D_Flip_Flop d_ff_6 (.D(E2), .clk(E2), .Q(d_ff_6_q), .reset(Rst));  // open: Qn, preset
  D_Flip_Flop d_ff_7 (.D(E3), .clk(E3), .Q(d_ff_7_q), .reset(Rst));  // open: Qn, preset
  or or_1 (or_1_out, edgetrigger_1_q, Rst);
  Dispenser dispenser_1 (
    .Activate(ENA_t), .Vend01(V1), .Vend02(V2), .Vend03(V3), .Restock01(stock1), .Restock02(stock2),
    .Restock03(stock3), .Availible1(pro1), .Availible2(pro2), .Availible3(pro3), .Empty1(empty1),
    .Empty2(empty2), .Empty3(empty3), .Dispenes1(dis1), .Dispenes2(dis2), .Dispenes3(dis3));
  Activator activator_1 (
    .InCash(bank_1_outacc), .Vend1(V1), .Vend2(V2), .Vend3(V3), .Reset(or_1_out), .CLK(CLK),
    .DepositeBCD(dipoBCd), .ChangeBCD(changeBCd), .activate(ENA_t), .out_10(N));
  and and_1 (and_1_out, CLK, d_ff_8_q);
  D_Flip_Flop d_ff_8 (.D(ENA_t), .clk(ENA_t), .Q(d_ff_8_q), .reset(Rst));  // open: Qn, preset
  message message_1 (
    .Rst(Rst), .in1(d_ff_1_q), .in2(d_ff_2_q), .in3(d_ff_3_q), .in5(d_ff_5_q), .in6(d_ff_6_q),
    .in7(d_ff_7_q), .Clk(and_1_out), .ttyOut(ttyOut));  // open: in4
  pogram pogram_1 (
    .Reset(Rst), .P1(dis1), .P2(dis2), .P3(dis3), .CLK(CLK), .TotalTimeBCD(Timer), .M1(A), .M2(B), .M3(C),
    .M4(D), .M5(E), .M6(F), .M7(G), .M8(H), .Done(Done));

  assign ttyR = Rst;

  // Other names for the same wires on the sheet: l1[7:0] = pro1; l2[7:0] = pro2; l3[7:0] = pro3
endmodule

module TextRAM (
);

  wire and_1_out, and_2_out, button_1_out, clk, clr_out, rd, rd_wrt_out, Rst_out, wrt;
  wire [6:0] keyboard_1_data;
  wire [7:0] controlled_buffer_2_out, counter_1_q, ram_1_data;

  Button u_clk (.out(clk));
  Button Rst (.out(Rst_out));
  Counter counter_1 (.clr(Rst_out), .clk(clk), .Q(counter_1_q));  // open: load, up, count, D, carry
  Button rd_wrt (.out(rd_wrt_out));
  T_Flip_Flop t_ff_1 (.T(1'b1), .clk(rd_wrt_out), .Q(wrt), .Qn(rd));  // open: reset, preset
  RAM #(.databus("bidir")) ram_1 (.addr(counter_1_q), .we(wrt), .oe(rd), .clk(clk), .data(ram_1_data));
  LED led_1 (.in(wrt));
  and and_1 (and_1_out, clk, wrt);
  Keyboard keyboard_1 (.clk(and_1_out), .clr(button_1_out), .data(keyboard_1_data));  // open: re, avail
  Button button_1 (.out(button_1_out));
  assign ram_1_data = wrt ? {1'b0, keyboard_1_data} : 8'bz;  // Controlled_Buffer controlled_buffer_1
  assign controlled_buffer_2_out = rd ? ram_1_data : 8'bz;  // Controlled_Buffer controlled_buffer_2
  and and_2 (and_2_out, clk, rd);
  TTY tty_1 (.data(controlled_buffer_2_out[6:0]), .clk(and_2_out), .clr(clr_out));  // open: we
  Button clr (.out(clr_out));
  LED led_2 (.in(rd));
endmodule
